# Fritzing sketch Complete_controller_Uno (using_pin_13) (saved by Fritzing 0.9.3b)

parts:
  S1 = Pushbutton [package=THT]
  S2 = Pushbutton [package=THT]
  S3 = Pushbutton [package=THT]
  S4 = Pushbutton [package=THT]
  S5 = Pushbutton [package=THT]
  S6 = Pushbutton [package=THT]
  S7 = Pushbutton [package=THT]
  S8 = Pushbutton [package=THT]
  S9 = Pushbutton [package=THT]
  S10 = Pushbutton [package=THT]
  S11 = Pushbutton [package=THT]
  S12 = Pushbutton [package=THT]
  R1 = Resistor [tolerance=±5% resistance=10k package=THT]
  R2 = Rotary Potentiometer (Small) [maximum_resistance=100kΩ package=THT]
  R3 = Rotary Potentiometer (Small) [maximum_resistance=100kΩ package=THT]
  R4 = Rotary Potentiometer (Small) [maximum_resistance=100kΩ package=THT]
  R5 = Rotary Potentiometer (Small) [maximum_resistance=100kΩ package=THT]
  R6 = Rotary Potentiometer (Small) [maximum_resistance=100kΩ package=THT]
  R7 = Rotary Potentiometer (Small) [maximum_resistance=100kΩ package=THT]
  Componente1 = Arduino Uno (Rev3)

nets:
  N1: S1.leg0, S2.leg0, S3.leg0, S4.leg0, S5.leg0, S6.leg0, S7.leg0, S8.leg0, S9.leg0, S11.leg0, S12.leg0, R1.Pin_1, R2.leg2, R3.leg2, R4.leg2, R5.leg2, R6.leg2, R7.leg2, Componente1.GND
  N2: S1.leg1, Componente1.D5_PWM
  N3: S2.leg1, Componente1.D4
  N4: S3.leg1, Componente1.D3_PWM
  N5: S4.leg1, Componente1.D2
  N6: S5.leg1, Componente1.D9_PWM
  N7: S6.leg1, Componente1.D6_PWM
  N8: S7.leg1, Componente1.D8
  N9: S8.leg1, Componente1.D7
  N10: S9.leg1, Componente1.D12/MISO
  N11: S10.leg0, R1.Pin_0, Componente1.D13/SCK
  N12: S10.leg1, R2.leg1, R3.leg1, R4.leg1, R5.leg1, R6.leg1, R7.leg1, Componente1.5V
  N13: S11.leg1, Componente1.D11_PWM/MOSI
  N14: S12.leg1, Componente1.D10_PWM/SS
  N15: R2.wiper, Componente1.A5/SCL
  N16: R3.wiper, Componente1.A4/SDA
  N17: R4.wiper, Componente1.A3
  N18: R5.wiper, Componente1.A2
  N19: R6.wiper, Componente1.A1
  N20: R7.wiper, Componente1.A0

notes:
  Use 10k resistor in the pin 13 button
