# Fritzing sketch  esquemático 2 (saved by Fritzing 0.9.3b)
breadboards: 1

parts:
  Part1 = Arduino Uno (Rev3)
  S1 = Pushbutton [package="[THT]"]
  S2 = Pushbutton [package="[THT]"]
  S3 = Pushbutton [package="[THT]"]
  R1 = TRIMPOT [package=3362u-2]
  R2 = TRIMPOT [package=3362u-2]

nets:
  N1: Part1.A0, R1.WIPER
  N2: Part1.A1, R2.WIPER
  N3: Part1.GND, S1.Pin_3, S1.Pin_4, S2.Pin_3, S2.Pin_4, S3.Pin_3, S3.Pin_4, R1.CCW, R2.CCW
  N4: Part1.D2, S3.Pin_1, S3.Pin_2
  N5: Part1.D3_PWM, S2.Pin_1, S2.Pin_2
  N6: Part1.D4, S1.Pin_1, S1.Pin_2
  N7: Part1.5V, R1.CW, R2.CW
