# Fritzing sketch esquemático 1 (saved by Fritzing 0.9.1b)
breadboards: 1

parts:
  Componente1 = Arduino Uno (Rev3)
  S1 = Pushbutton [package="[THT]"]
  S2 = Pushbutton [package="[THT]"]
  S3 = Pushbutton [package="[THT]"]
  S4 = Pushbutton [package="[THT]"]
  R1 = Rotary Potentiometer (Small) [maximum_resistance=100kΩ package=THT]

nets:
  N1: Componente1.A0, R1.wiper
  N2: Componente1.GND, S1.Pin_1, S1.Pin_2, S2.Pin_1, S2.Pin_2, S3.Pin_1, S3.Pin_2, S4.Pin_1, S4.Pin_2, R1.leg1
  N3: Componente1.D2, S1.Pin_3, S1.Pin_4
  N4: Componente1.D3_PWM, S3.Pin_3, S3.Pin_4
  N5: Componente1.D4, S2.Pin_3, S2.Pin_4
  N6: Componente1.D5_PWM, S4.Pin_3, S4.Pin_4
  N7: Componente1.5V, R1.leg2
